// Digital circuit Next_State_FSM.dig as structural Verilog
module Next_State_FSM (
  input  [8:0] Cur,
  input  [3:0] Op,
  output [8:0] New
);

  wire demultiplexer_1_out_0, nor_1_out, not_1_out, or_1_out;

  Demultiplexer #(.Selector_Bits(2)) demultiplexer_1 (
    .sel(Op[3:2]), .in(Cur[8]), .out_0(demultiplexer_1_out_0), .out_1(New[3]), .out_2(New[1]));  // open: out_3
  not not_1 (not_1_out, Op[0]);
  Demultiplexer demultiplexer_2 (.sel(not_1_out), .in(Cur[3]), .out_0(New[4]), .out_1(New[5]));
  Demultiplexer demultiplexer_3 (.sel(Op[0]), .in(demultiplexer_1_out_0), .out_0(New[6]), .out_1(New[7]));
  nor nor_1 (nor_1_out, Cur[0], Cur[1], Cur[2], Cur[3], Cur[4], Cur[5], Cur[6], Cur[7], Cur[8]);
  or or_1 (or_1_out, Cur[7], Cur[6], Cur[5], Cur[4], Cur[2]);
  or or_2 (New[0], nor_1_out, or_1_out);

  assign {New[8], New[2]} = {Cur[0], Cur[1]};

  // Notes on the sheet:
  //   0=Fetch,
  //   1=ExeReg,
  //   2=ALUWB,
  //   3=MemADR,
  //   4=WriteToReg,
  //   5=WriteToMem,
  //   6=WriteImm8
  //   7=SethImm8
  //   8=Decode
  //   One-Hot encoding
  //   0-indexed
  //   0=movl,
  //   1=seth
  //   Fetch
  //   Init
endmodule

/* Test case NextStateLogic:
Op	Cur	New
0b1000	0x01	0x02
0b0001	0x01	0x80
*/
