// Digital circuit Output_Logic_FSM.dig as structural Verilog
// Converts an input state to control lines
module Output_Logic_FSM (
  input  [8:0] In,
  output FlagW,
  output MemWE,
  output RegWE,
  output ALUWE,
  output InstWE,
  output MemSrc,
  output [1:0] ALUSrcA,
  output [1:0] ALUSrcB,
  output [1:0] ResSrc,
  output [1:0] ALUOP
);

  or or_1 (RegWE, In[0], In[2], In[4], In[6], In[7]);
  or or_2 (ALUWE, In[1], In[3]);
  or or_3 (MemSrc, In[3], In[5]);
  or or_4 (ALUSrcA[0], In[1], In[7]);
  or or_5 (ALUSrcA[1], In[3], In[6]);
  or or_6 (ALUSrcB[0], In[6], In[7]);
  or or_7 (ALUSrcB[1], In[0], In[7]);
  or or_8 (ResSrc[0], In[4], In[7]);
  or or_9 (ResSrc[1], In[0], In[3], In[6], In[7]);

  assign ALUOP = {In[7], 1'b0};
  assign FlagW = In[1];
  assign InstWE = In[0];
  assign MemWE = In[5];

  // Notes on the sheet:
  //   0=Fetch,
  //   1=ExeReg,
  //   2=ALUWB,
  //   3=MemADR,
  //   4=WriteToReg,
  //   5=WriteToMem,
  //   6=WriteImm8
  //   7=SethImm8
  //   8=Decode
  //   8, .7, .6, 5, .4, .3, 2, .1, .0
  //   0=Fetch,
  //   1=ExeReg,
  //   2=ALUWB,
  //   3=MemADR,
  //   4=WriteToReg,
  //   5=WriteToMem,
  //   6=WriteImm8
  //   7=SethImm8
  //   One-Hot encoding
  //   0-indexed
  //   Same for now; might change
  //   with more extensions added
  //   This goes to the Decoder :)
endmodule
