// Digital circuit RegWS_FSM.dig as structural Verilog
module RegWS_FSM (
  input  [2:0] RD,
  input  [8:0] State,
  output [2:0] RegWS
);

  wire [2:0] notconnected_1_out;

  Multiplexer #(.Bits(3), .Selector_Bits(2)) multiplexer_1 (
    .sel({State[8], State[0]}), .in_0(RD), .in_1(3'b110), .in_2(3'b101), .in_3(notconnected_1_out),
    .out(RegWS));
  // NotConnected on notconnected_1_out

  // Notes on the sheet:
  //   Spooky I know,
  //   Fetch = leastsig bit
  //   WriteFlags=Mostsig
  //   one-hot so never both
  //   0=Fetch,
  //   1=ExeReg,
  //   2=ALUWB,
  //   3=MemADR,
  //   4=WriteToReg,
  //   5=WriteToMem,
  //   6=WriteImm8
  //   7=SethImm8
  //   8=WriteFlags
endmodule
