// Digital circuit control_unit.dig as structural Verilog
module control_unit (
  input  [15:0] INST,
  input  [15:0] FLGS,
  output [1:0] ALUOP,
  output [1:0] DMUX,
  output [2:0] RS1,
  output [2:0] RS2,
  output [2:0] WS,
  output WE,
  output FLEN,
  output SETH,
  output EXEC,
  output STR,
  output LDR
);

  wire and_1_out, nor_1_out, nor_2_out, not_1_out;
  wire [1:0] notconnected_1_out;

  Multiplexer #(.Selector_Bits(2), .Bits(2)) multiplexer_1 (
    .sel(INST[15:14]), .in_0(2'b10), .in_1(2'b01), .in_2(2'b00), .in_3(notconnected_1_out), .out(DMUX));
  // NotConnected on notconnected_1_out
  nor nor_1 (nor_1_out, INST[12], INST[13]);
  and and_1 (and_1_out, DMUX[0], nor_1_out);
  nor nor_2 (nor_2_out, DMUX[0], DMUX[1]);
  and and_2 (EXEC, ~FLGS[0], INST[11]);  // And
  and and_3 (SETH, INST[12], DMUX[1]);
  nor nor_3 (WE, EXEC, and_1_out);
  and and_4 (STR, and_1_out, ~EXEC);  // And
  and and_5 (FLEN, nor_2_out, ~EXEC);  // And
  Multiplexer #(.Bits(3)) multiplexer_2 (.sel(not_1_out), .in_0(INST[10:8]), .in_1(INST[2:0]), .out(RS2));
  not not_1 (not_1_out, DMUX[0]);

  assign ALUOP = INST[13:12];
  assign LDR = DMUX[0];
  assign RS1 = INST[6:4];
  assign WS = INST[10:8];

  // Notes on the sheet:
  //   EXEC: If High, the command was not executed
  //   Z
  //   00 = 2 I format
  //   01 = 1 R format Mem
  //   10 = 0 R format ALU
  //   Rd
  //   Ra
  //   Rb
endmodule

/* Test case All Tests:
	INST                                    WE  ALUOP  RS1   RS2  WS  STR  LDR DMUX FLEN

let aluop  = 0b1000;
let ldrop  = 0b0101;
let strop  = 0b0100;
let movlop = 0b0000;

loop(rd, 1<<3)
loop(ra, 1<<3)
loop(rb, 1<<3)

loop(i, 4)
	((aluop+i)<<12 | rd<<8 | ra<<4 | rb<<0) 1  (i)     (ra)  (rb) (rd)  0   X    0  1 #test add/sub/and/xor
end loop

	(ldrop    <<12 | rd<<8 | ra<<4 )        1  X       (ra)  x    (rd)  0   1    1  0 #test ldr
	(strop    <<12 | rd<<8 | ra<<4 )        0  X       (ra)  (rd)  X    1   X    X  0 #test str
	
	let imm = random(256);
	(movlop   <<12 | rd<<8 | imm )          1  X       X      X   (rd)  0   X    2  0 #test movl

end loop
end loop
end loop
*/

/* Test case WS:
	INST                                    WS 

let aluop  = 0b1000;
let ldrop  = 0b0101;
let strop  = 0b0100;
let movlop = 0b0000;

loop(rd, 1<<3)
loop(ra, 1<<3)
loop(rb, 1<<3)

loop(i, 4)
	((aluop+i)<<12 | rd<<8 | ra<<4 | rb<<0) (rd)  #test add/sub/and/xor
end loop

	(ldrop    <<12 | rd<<8 | ra<<4 )        (rd)   #test ldr
	(strop    <<12 | rd<<8 | ra<<4 )        X     #test str
	
	let imm = random(256);
	(movlop   <<12 | rd<<8 | imm )          (rd)  #test movl

end loop
end loop
end loop
*/

/* Test case RS1:
	INST                                    RS1  

let aluop  = 0b1000;
let ldrop  = 0b0101;
let strop  = 0b0100;
let movlop = 0b0000;

loop(rd, 1<<3)
loop(ra, 1<<3)
loop(rb, 1<<3)

loop(i, 4)
	((aluop+i)<<12 | rd<<8 | ra<<4 | rb<<0) (ra)  #test add/sub/and/xor
end loop

	(ldrop    <<12 | rd<<8 | ra<<4 )        (ra)  #test ldr
	(strop    <<12 | rd<<8 | ra<<4 )        (ra)  #test str

end loop
end loop
end loop
*/

/* Test case RS2:
	INST                                    RS2  

let aluop  = 0b1000;
let ldrop  = 0b0101;
let strop  = 0b0100;
let movlop = 0b0000;

loop(rd, 1<<3)
loop(ra, 1<<3)
loop(rb, 1<<3)

loop(i, 4)
	((aluop+i)<<12 | rd<<8 | ra<<4 | rb<<0) (rb) #test add/sub/and/xor
end loop
	(strop    <<12 | rd<<8 | ra<<4 )        (rd) #test str

end loop
end loop
end loop
*/

/* Test case STR:
	INST                                    STR 

let aluop  = 0b1000;
let ldrop  = 0b0101;
let strop  = 0b0100;
let movlop = 0b0000;

loop(rd, 1<<3)
loop(ra, 1<<3)
loop(rb, 1<<3)

loop(i, 4)
	((aluop+i)<<12 | rd<<8 | ra<<4 | rb<<0) 0  #test add/sub/and/xor
end loop

	(ldrop    <<12 | rd<<8 | ra<<4 )        0  #test ldr
	(strop    <<12 | rd<<8 | ra<<4 )        1  #test str
	
	let imm = random(256);
	(movlop   <<12 | rd<<8 | imm )          0  #test movl

end loop
end loop
end loop
*/

/* Test case WE:
	INST                                    WE  

let aluop  = 0b1000;
let ldrop  = 0b0101;
let strop  = 0b0100;
let movlop = 0b0000;

loop(rd, 1<<3)
loop(ra, 1<<3)
loop(rb, 1<<3)

loop(i, 4)
	((aluop+i)<<12 | rd<<8 | ra<<4 | rb<<0) 1  #test add/sub/and/xor
end loop

	(ldrop    <<12 | rd<<8 | ra<<4 )        1  #test ldr
	(strop    <<12 | rd<<8 | ra<<4 )        0  #test str
	
	let imm = random(256);
	(movlop   <<12 | rd<<8 | imm )          1  #test movl

end loop
end loop
end loop
*/

/* Test case LDR:
	INST                                    LDR 

let aluop  = 0b1000;
let ldrop  = 0b0101;
let strop  = 0b0100;
let movlop = 0b0000;

loop(rd, 1<<3)
loop(ra, 1<<3)
loop(rb, 1<<3)

loop(i, 4)
	((aluop+i)<<12 | rd<<8 | ra<<4 | rb<<0) X    #test add/sub/and/xor
end loop

	(ldrop    <<12 | rd<<8 | ra<<4 )        1    #test ldr
	(strop    <<12 | rd<<8 | ra<<4 )        X    #test str
	
	let imm = random(256);
	(movlop   <<12 | rd<<8 | imm )          X    #test movl

end loop
end loop
end loop
*/

/* Test case DMUX:
	INST                                    DMUX

let aluop  = 0b1000;
let ldrop  = 0b0101;
let strop  = 0b0100;
let movlop = 0b0000;

loop(rd, 1<<3)
loop(ra, 1<<3)
loop(rb, 1<<3)

loop(i, 4)
	((aluop+i)<<12 | rd<<8 | ra<<4 | rb<<0) 0  #test add/sub/and/xor
end loop

	(ldrop    <<12 | rd<<8 | ra<<4 )        1  #test ldr
	
	let imm = random(256);
	(movlop   <<12 | rd<<8 | imm )          2  #test movl

end loop
end loop
end loop
*/

/* Test case ALUOP:
	INST                                    ALUOP 

let aluop  = 0b1000;
let ldrop  = 0b0101;
let strop  = 0b0100;
let movlop = 0b0000;

loop(rd, 1<<3)
loop(ra, 1<<3)
loop(rb, 1<<3)

loop(i, 4)
	((aluop+i)<<12 | rd<<8 | ra<<4 | rb<<0) (i)    #test add/sub/and/xor
end loop

end loop
end loop
end loop
*/

/* Test case FLEN:
	INST                                 FLEN

let aluop  = 0b1000;
let ldrop  = 0b0101;
let strop  = 0b0100;
let movlop = 0b0000;

loop(rd, 1<<3)
loop(ra, 1<<3)
loop(rb, 1<<3)

loop(i, 4)
	(aluop <<12 | rd<<8 | ra<<4) 1 #ALU
end loop

	(ldrop    <<12 | rd<<8 | ra<<4 ) 0 #test ldr
	(strop    <<12 | rd<<8 | ra<<4 ) 0 #test str
	
	let imm = random(256);
	(movlop   <<12 | rd<<8 | imm ) 0 #test movl

end loop
end loop
end loop
*/
