// Digital circuit extended-control_unit.dig as structural Verilog
module extended_control_unit (
  input  CLK,
  input  [3:0] Op,
  input  CondBit,
  input  [2:0] Rd,
  input  [3:0] Flags,
  output MemSrc,
  output MemWE,
  output InstWE,
  output [1:0] ResSrc,
  output FLWE,
  output ALUWE,
  output [1:0] ALUOP,
  output [1:0] ALUSrcB,
  output [1:0] ALUSrcA,
  output [2:0] RegWS,
  output RegWE
);

  wire and_2_out, and_7_out, No, output_logic_fsm_1_aluwe, output_logic_fsm_1_flagw,
       output_logic_fsm_1_memwe, output_logic_fsm_1_regwe;
  wire [1:0] output_logic_fsm_1_aluop;
  wire [3:0] FLInControl_q;
  wire [8:0] next_state_fsm_1_new, Sta;

  Register #(.Bits(4)) FLInControl (.D(Flags), .C(CLK), .en(1'b1), .Q(FLInControl_q));
  Next_State_FSM next_state_fsm_1 (.Cur(Sta), .Op(Op), .New(next_state_fsm_1_new));
  RegWS_FSM regws_fsm_1 (.RD(Rd), .State(Sta), .RegWS(RegWS));
  Register #(.Bits(9)) State (.D(next_state_fsm_1_new), .C(CLK), .en(1'b1), .Q(Sta));
  and and_1 (No, ~FLInControl_q[0], CondBit);  // And
  Output_Logic_FSM output_logic_fsm_1 (
    .In(Sta), .FlagW(output_logic_fsm_1_flagw), .MemWE(output_logic_fsm_1_memwe),
    .RegWE(output_logic_fsm_1_regwe), .ALUWE(output_logic_fsm_1_aluwe), .InstWE(InstWE), .MemSrc(MemSrc),
    .ALUSrcA(ALUSrcA), .ALUSrcB(ALUSrcB), .ResSrc(ResSrc), .ALUOP(output_logic_fsm_1_aluop));
  and and_2 (and_2_out, No, ~InstWE);  // And
  and and_3 (FLWE, ~No, output_logic_fsm_1_flagw);  // And
  and and_4 (MemWE, output_logic_fsm_1_memwe, ~No);  // And
  and and_5 (RegWE, output_logic_fsm_1_regwe, ~and_2_out);  // And
  and and_6 (ALUWE, output_logic_fsm_1_aluwe, ~No);  // And
  Multiplexer #(.Bits(2)) multiplexer_1 (.sel(and_7_out), .in_0(output_logic_fsm_1_aluop), .in_1(Op[1:0]), .out(ALUOP));
  and and_7 (and_7_out, Op[3], ~Sta[0]);  // And

  // Notes on the sheet:
  //   Rd: The register to write to via RegWS
  //   Cond Check
  //   ALU Decode
  //   Without branches, 
  //   this is literally just fetch
  //   which isn't conditional
endmodule
