// Digital circuit extended-cpu.dig as structural Verilog
module extended_cpu (
  input  CLK
);

  wire extended_control_unit_1_aluwe, extended_control_unit_1_flwe, extended_control_unit_1_instwe,
       extended_control_unit_1_memsrc, extended_control_unit_1_memwe, extended_control_unit_1_regwe;
  wire [1:0] extended_control_unit_1_aluop, extended_control_unit_1_alusrca, extended_control_unit_1_alusrcb,
       extended_control_unit_1_ressrc;
  wire [2:0] extended_control_unit_1_regws, INST_q, INST_q_3, INST_q_4, multiplexer_2_out, multiplexer_3_out;
  wire [3:0] extended_alu_1_flag, INST_q_5, TempFlag_q;
  wire [7:0] extended_alu_1_result;
  wire [11:3] INST_q_2;
  wire [15:0] ALURes_q, extended_reg_file_1_out1, extended_reg_file_1_out2, extended_reg_file_1_pc,
       multiplexer_1_out, multiplexer_4_out, multiplexer_5_out, multiplexer_6_out, notconnected_1_out,
       R_WData_q, RAM_d, register_1_q, register_2_q;
  wire [15:8] extended_alu_1_result_2;

  Multiplexer #(.Bits(16)) multiplexer_1 (
    .sel(extended_control_unit_1_memsrc), .in_0(extended_reg_file_1_pc), .in_1(multiplexer_6_out),
    .out(multiplexer_1_out));
  RAMDualPort #(.AddrBits(16), .isProgramMemory("true"), .Bits(16)) RAM (
    .A(multiplexer_1_out), .Din(extended_reg_file_1_out1), .str(extended_control_unit_1_memwe), .C(CLK),
    .ld(1'b1), .D(RAM_d));
  Register #(.Bits(16)) INST (
    .D(RAM_d), .C(CLK), .en(extended_control_unit_1_instwe),
    .Q({INST_q_5, INST_q_2[11], INST_q_4, INST_q_2[7], INST_q_3, INST_q_2[3], INST_q}));
  Register #(.Bits(16)) R_WData (.D(RAM_d), .C(CLK), .en(1'b1), .Q(R_WData_q));
  extended_control_unit extended_control_unit_1 (
    .CLK(CLK), .Op(INST_q_5), .CondBit(INST_q_2[11]), .Rd(INST_q_4), .Flags(TempFlag_q),
    .MemSrc(extended_control_unit_1_memsrc), .MemWE(extended_control_unit_1_memwe),
    .InstWE(extended_control_unit_1_instwe), .ResSrc(extended_control_unit_1_ressrc),
    .FLWE(extended_control_unit_1_flwe), .ALUWE(extended_control_unit_1_aluwe),
    .ALUOP(extended_control_unit_1_aluop), .ALUSrcB(extended_control_unit_1_alusrcb),
    .ALUSrcA(extended_control_unit_1_alusrca), .RegWS(extended_control_unit_1_regws),
    .RegWE(extended_control_unit_1_regwe));
  Multiplexer #(.Bits(3)) multiplexer_2 (.sel(INST_q_5[3]), .in_0(INST_q_4), .in_1(INST_q_3), .out(multiplexer_2_out));
  Multiplexer #(.Bits(3)) multiplexer_3 (.sel(INST_q_5[3]), .in_0(INST_q_3), .in_1(INST_q), .out(multiplexer_3_out));
  extended_reg_file extended_reg_file_1 (
    .WS(extended_control_unit_1_regws), .WE(extended_control_unit_1_regwe), .RS1(multiplexer_2_out),
    .RS2(multiplexer_3_out), .IN(multiplexer_6_out), .clk(CLK), .Flags(TempFlag_q),
    .OUT1(extended_reg_file_1_out1), .PC(extended_reg_file_1_pc), .OUT2(extended_reg_file_1_out2));
  Register #(.Bits(16)) register_1 (.D(extended_reg_file_1_out1), .C(CLK), .en(1'b1), .Q(register_1_q));
  Register #(.Bits(16)) register_2 (.D(extended_reg_file_1_out2), .C(CLK), .en(1'b1), .Q(register_2_q));
  Multiplexer #(.Selector_Bits(2), .Bits(16)) multiplexer_4 (
    .sel(extended_control_unit_1_alusrca), .in_0(extended_reg_file_1_pc), .in_1(register_1_q),
    .in_2({16{1'b0}}), .in_3(notconnected_1_out), .out(multiplexer_4_out));
  // NotConnected on notconnected_1_out
  Multiplexer #(.Selector_Bits(2), .Bits(16)) multiplexer_5 (
    .sel(extended_control_unit_1_alusrcb), .in_0(register_2_q),
    .in_1({{8{1'b0}}, INST_q_2[7], INST_q_3, INST_q_2[3], INST_q}), .in_2(16'h1), .in_3({16{1'b1}}),
    .out(multiplexer_5_out));
  extended_ALU extended_alu_1 (
    .ALUOP(extended_control_unit_1_aluop), .A(multiplexer_4_out), .B(multiplexer_5_out),
    .FLAG(extended_alu_1_flag), .RESULT({extended_alu_1_result_2, extended_alu_1_result}));
  Register #(.Bits(4)) TempFlag (.D(extended_alu_1_flag), .C(CLK), .en(extended_control_unit_1_flwe), .Q(TempFlag_q));
  Register #(.Bits(16)) ALURes (
    .D({extended_alu_1_result_2, extended_alu_1_result}), .C(CLK), .en(extended_control_unit_1_aluwe),
    .Q(ALURes_q));
  Multiplexer #(.Selector_Bits(2), .Bits(16)) multiplexer_6 (
    .sel(extended_control_unit_1_ressrc), .in_0(ALURes_q), .in_1(R_WData_q),
    .in_2({extended_alu_1_result_2, extended_alu_1_result}),
    .in_3({INST_q_2[7], INST_q_3, INST_q_2[3], INST_q, extended_alu_1_result}), .out(multiplexer_6_out));

  // Notes on the sheet:
  //   Would put PC here if 
  //   not for Reading PC in QuAC
endmodule

/* Test case CPU:
# assert these registers can be tested
CLK R1 R2 R3 R4 FL PC

program(0)  # assert program memory exists
init R1=0;  # assert we can initialise R1
init R2=0;  # assert we can initialise R2
init R3=0;  # assert we can initialise R3
init R4=0;  # assert we can initialise R4
init FL=0;  # assert we can initialise FL
init PC=0;  # assert we can initialise PC

0 0 0 0 0 0 0
*/

/* Test case GP_PC:
CLK     R1     R2     R3     R4     PC

init R1=0x5;
init R2=0x98;
c        x      x      x      x 0x0000 # overhead
c        x      x      x      x      x # 3 Cycles ALU
c   	 x      x      x      x      x
c   	 x      x      x      x      x
c   0x0005 0x0098      x      x 0x0001
c        x      x      x      x      x # 3 Cycles ALU
c   	 x      x      x      x      x
c   	 x      x      x      x      x
c   0x0005 0x0098      x      x 0x0002
c        x      x      x      x      x # 3 Cycles ALU
c   	 x      x      x      x      x
c   	 x      x      x      x      x
c   0x0005 0x0002      x      x 0x0003
c        x      x      x      x      x # 3 Cycles ALU
c   	 x      x      x      x      x
c   	 x      x      x      x      x
c   0x0005 0x0002      x      x 0x0005
c        x      x      x      x      x # 2 Cycles I-Mem
c   	 x      x      x      x      x
program(0x8000,0x8000,0x8260,0x8610,0x03ff,0x0000)
*/

/* Test case MOVL:
CLK     R1     R2     R3     R4     PC

c        x      x      x      x 0x0000 # Overhead
c        x      x      x      x      x # 2 Cycles each
c   	 x      x      x      x      x
c   0x00ff	x      x      x 0x0001
c        x      x      x      x      x # 2 Cycles each
c   	 x      x      x      x      x
c   0x0000      x      x      x 0x0002
c        x      x      x      x      x # 2 Cycles each
c   	 x      x      x      x      x
c   0x0000 0x000c      x      x 0x0003
c        x      x      x      x      x # 2 Cycles each
c   	 x      x      x      x      x
c   0x0000 0x000c 0x000d      x 0x0004
c        x      x      x      x      x # 2 Cycles each
c   	 x      x      x      x      x
c   0x0000 0x000c 0x000d 0x00a3 0x0005

program(0x01ff,0x0100,0x020c,0x030d,0x04a3)
*/

/* Test case READ_FLAGS:
CLK     R1     R2     R3     R4     PC

init R1=0x76;
init R4=0xF;
c        x      x      x      x 0x0000 # overhead
c        x      x      x      x      x # 3 Cycles ALU
c   	 x      x      x      x      x
c   	 x      x      x      x      x
c   0x0076 0x0000      x 0x000f 0x0001
c        x      x      x      x      x # 3 Cycles ALU
c   	 x      x      x      x      x
c   	 x      x      x      x      x
c   0x0076 0x0000      x 0x000f 0x0002
c        x      x      x      x      x # 3 Cycles ALU
c   	 x      x      x      x      x
c   	 x      x      x      x      x
c   0x0076 0x0000 0x0005 0x000f 0x0003

program(0x9211,0x8350,0xa334)
*/

/* Test case SETH:
CLK     R1     R2     R3     R4     PC

init R1=0xAD;
init R2=0x0D;
init R3=0xEF;
init R4=0xAD;
c        x      x      x      x 0x0000 # Overhead
c        x      x      x      x      x # 2 Cycles each
c   	 x      x      x      x      x
c   0xdead 0x000d 0x00ef 0x00ad 0x0001
c        x      x      x      x      x # 2 Cycles each
c   	 x      x      x      x      x
c   0xdead 0xf00d 0x00ef 0x00ad 0x0002
c        x      x      x      x      x # 2 Cycles each
c   	 x      x      x      x      x
c   0xdead 0xf00d 0xbeef 0x00ad 0x0003
c        x      x      x      x      x # 2 Cycles each
c   	 x      x      x      x      x
c   0xdead 0xf00d 0xbeef 0x0bad 0x0004
c        x      x      x      x      x # 2 Cycles each
c   	 x      x      x      x      x

program(0x11de,0x12f0,0x13be,0x140b)
*/

/* Test case FLAGS:
CLK     R1     R2     R3     R4   FLAG     PC

declare FLAG = FL & 0xF;

init R1=1;
init R2=0xFFFF;
init R3=0x7FFF;
init R4=0x8000;
c        x      x      x      x      x 0x0000 #overhead
c        x      x      x      x      x      x # 3 Cycles ALU
c   	 x      x      x      x      x      x
c   	 x      x      x      x      x      x
c   0x0001 0xffff 0x7fff 0x8000 0x0001 0x0001
c        x      x      x      x      x      x # 3 Cycles ALU
c   	 x      x      x      x      x      x
c   	 x      x      x      x      x      x
c   0x0001 0xffff 0x7fff 0x8000 0x0005 0x0002
c        x      x      x      x      x      x # 3 Cycles ALU
c   	 x      x      x      x      x      x
c   	 x      x      x      x      x      x
c   0x0001 0xffff 0x7fff 0x8000 0x0005 0x0003
c        x      x      x      x      x      x # 3 Cycles ALU
c   	 x      x      x      x      x      x
c   	 x      x      x      x      x      x
c   0x0001 0xffff 0x7fff 0x8000 0x0000 0x0004
c        x      x      x      x      x      x # 3 Cycles ALU
c   	 x      x      x      x      x      x
c   	 x      x      x      x      x      x
c   0x0001 0xffff 0x7fff 0x8000 0x0006 0x0005
c        x      x      x      x      x      x # 3 Cycles ALU
c   	 x      x      x      x      x      x
c   	 x      x      x      x      x      x
c   0x0001 0xffff 0x7fff 0x8000 0x0006 0x0006
c        x      x      x      x      x      x # 3 Cycles ALU
c   	 x      x      x      x      x      x
c   	 x      x      x      x      x      x
c   0x0001 0xffff 0x7fff 0x8000 0x0002 0x0007
c        x      x      x      x      x      x # 3 Cycles ALU
c   	 x      x      x      x      x      x
c   	 x      x      x      x      x      x
c   0x0001 0xffff 0x7fff 0x8000 0x0002 0x0008
c        x      x      x      x      x      x # 3 Cycles ALU
c   	 x      x      x      x      x      x
c   	 x      x      x      x      x      x
c   0x0001 0xffff 0x7fff 0x8000 0x000c 0x0009
c        x      x      x      x      x      x # 3 Cycles ALU
c   	 x      x      x      x      x      x
c   	 x      x      x      x      x      x
c   0x0001 0xffff 0x7fff 0x8000 0x0004 0x000a
c        x      x      x      x      x      x # 3 Cycles ALU
c   	 x      x      x      x      x      x
c   	 x      x      x      x      x      x
c   0x0001 0xffff 0x7fff 0x8000 0x000c 0x000b
c        x      x      x      x      x      x # 3 Cycles ALU
c   	 x      x      x      x      x      x
c   	 x      x      x      x      x      x
c   0x0001 0xffff 0x7fff 0x8000 0x000a 0x000c


program(0x8000,0x8012,0x9011,0x9012,0x8022,0x9021,0x8034,0x8041,0x9041,0x9031,0x9043,0x8013)
*/

/* Test case LDR:
CLK     R1     R2     R3     R4     PC

init R1=0x3;
c        x      x      x      x 0x0000 # overhead
c        x      x      x      x      x # 3 Cycles each
c   	 x      x      x      x      x
c   	 x      x      x      x      x
c   0x0003 0x5200      x      x 0x0001
c        x      x      x      x      x # 3 Cycles each
c   	 x      x      x      x      x
c   	 x      x      x      x      x
c   0x0003 0x5200 0x9876      x 0x0002


program(0x5200,0x5310,0x0000,0x9876)
*/

/* Test case ALU:
CLK     R1     R2     R3     R4   FLAG     PC

declare FLAG = FL & 0xF;

init R1=0x1A;
init R2=0xF000;
init R2=0xCDFF;
c        x      x      x      x      x 0x0000 # overhead
c        x      x      x      x      x      x # 3 Cycles ALU
c   	 x      x      x      x      x      x
c   	 x      x      x      x      x      x
c   0x001a 0xcdff      x 0xce19 0x0002 0x0001
c        x      x      x      x      x      x # 3 Cycles ALU
c   	 x      x      x      x      x      x
c   	 x      x      x      x      x      x
c   0x001a 0xcdff      x 0x001a 0x0000 0x0002
c        x      x      x      x      x      x # 3 Cycles ALU
c   	 x      x      x      x      x      x
c   	 x      x      x      x      x      x
c   0x001a 0xcdff      x 0xcdff 0x0006 0x0003
c        x      x      x      x      x      x # 3 Cycles ALU
c   	 x      x      x      x      x      x
c   	 x      x      x      x      x      x
c   0x001a 0xcdff      x 0x3201 0x0000 0x0004
c        x      x      x      x      x      x # 3 Cycles ALU
c   	 x      x      x      x      x      x
c   	 x      x      x      x      x      x
c   0x001a 0xcdff      x 0x0000 0x0001 0x0005
c        x      x      x      x      x      x # 3 Cycles ALU
c   	 x      x      x      x      x      x
c   	 x      x      x      x      x      x
c   0x001a 0xcdff      x 0x0000 0x0001 0x0006
c        x      x      x      x      x      x # 3 Cycles ALU
c   	 x      x      x      x      x      x
c   	 x      x      x      x      x      x
c   0x001a 0xcdff      x 0xcde5 0x0002 0x0007
c        x      x      x      x      x      x # 3 Cycles ALU
c   	 x      x      x      x      x      x
c   	 x      x      x      x      x      x
c   0x001a 0xcdff      x 0xcde5 0x0002 0x0008
c        x      x      x      x      x      x # 3 Cycles ALU
c   	 x      x      x      x      x      x
c   	 x      x      x      x      x      x
c   0x0000 0xcdff      x 0xcde5 0x0001 0x0009
c        x      x      x      x      x      x # 3 Cycles ALU
c   	 x      x      x      x      x      x
c   	 x      x      x      x      x      x
c   0x0000 0x0000      x 0xcde5 0x0001 0x000a

program(0x8412,0xa421,0x9423,0x9432,0xa413,0xa431,0xb412,0xb012,0x8100,0x8230)
*/

/* Test case STR:
CLK     R1     R2     R3     R4     PC

init R1=0x3;
init R2=0xDAF5;
c        x      x      x      x 0x0000 # overhead
c        x      x      x      x      x # 3 Cycles each
c   	 x      x      x      x      x
c   	 x      x      x      x      x
c   0x0003 0xdaf5      x      x 0x0001
c        x      x      x      x      x # 3 Cycles each
c   	 x      x      x      x      x
c   	 x      x      x      x      x
c   0x0003 0xdaf5 0xdaf5      x 0x0002

program(0x4210,0x5310,0x0000,0x0000)
*/

/* Test case JUMPS:
CLK     R1     R2     R3     R4     PC

c        x      x      x      x 0x0000 # overhead
c        x      x      x      x      x # 2 Cycles I-Mem
c   	 x      x      x      x      x
c        x      x      x 0x0003 0x0001
c        x      x      x      x      x # 3 Cycles ALU
c   	 x      x      x      x      x
c   	 x      x      x      x      x
c   0x0001      x      x 0x0003 0x0002
c        x      x      x      x      x # 3 Cycles ALU
c   	 x      x      x      x      x
c   	 x      x      x      x      x
c   0x0001      x      x 0x0003 0x0005
c        x      x      x      x      x # 2 Cycles I-Mem
c   	 x      x      x      x      x
c   0x0001      x 0x0003 0x0003 0x0006
c        x      x      x      x      x # 3 Cycles ALU
c   	 x      x      x      x      x
c   	 x      x      x      x      x
c   0x0001      x 0x0003 0x0003 0x0003
c        x      x      x      x      x # 2 Cycles I-Mem
c   	 x      x      x      x      x
c   0x0001 0x0003 0x0003 0x0003 0x0004
c        x      x      x      x      x # 3 Cycles ALU
c   	 x      x      x      x      x
c   	 x      x      x      x      x
c   0x0001 0x0003 0x0003 0x0003 0x0007
c        x      x      x      x      x # 2 Cycles I-Mem
c   	 x      x      x      x      x
c   0x0001 0x0003 0x0003 0x0009 0x0008
c        x      x      x      x      x # 3 Cycles ALU
c   	 x      x      x      x      x
c   	 x      x      x      x      x
c   0x0001 0x0003 0x0003 0x0009 0x000a

program(0x0403,0x8160,0x8664,0x0203,0x8662,0x0303,0x9663,0x0409,0x8614,0x8660,0x0000)
*/

/* Test case ADD:
CLK     R1     R2     R3     R4     PC

init R1=0x87;
init R2=0x93;
c        x      x      x      x 0x0000 # Overhead
c        x      x      x      x      x # 3 Cycles each
c   	 x      x      x      x      x
c   	 x      x      x      x      x
c   0x0087 0x0093 0x011a      x 0x0001
c        x      x      x      x      x # 3 Cycles each
c   	 x      x      x      x      x
c   	 x      x      x      x      x
c   0x0087 0x0093 0x011a 0x01ad 0x0002
c        x      x      x      x      x # 3 Cycles each
c   	 x      x      x      x      x
c   	 x      x      x      x      x
c   0x010e 0x0093 0x011a 0x01ad 0x0003

program(0x8321,0x8432,0x8111)
*/

/* Test case REC:
CLK     R1     R2     R3     R4     PC

c        x      x      x      x 0x0000 # overhead
c   	 x      x      x      x      x # 3 cycles
c   	 x      x      x      x      x 
c   	 x      x      x      x      x 
c        x      x      x 0x0000 0x0001
c   	 x      x      x      x      x # 2 cycles
c   	 x      x      x      x      x 
c   0x0020      x      x 0x0000 0x0002
c   	 x      x      x      x      x # 3 cycles
c   	 x      x      x      x      x 
c   	 x      x      x      x      x 
c   0x0020 0x0008      x 0x0000 0x0003
c   	 x      x      x      x      x # 2 cycles
c   	 x      x      x      x      x 
c   0x0020 0x0008 0x0001 0x0000 0x0004
c   	 x      x      x      x      x # 3 cycles
c   	 x      x      x      x      x 
c   	 x      x      x      x      x 
c   0x0021 0x0008 0x0001 0x0000 0x0005
c   	 x      x      x      x      x # 3 cycles
c   	 x      x      x      x      x 
c   	 x      x      x      x      x 
c   0x0021 0x0008 0x0001 0xffff 0x0006
c   	 x      x      x      x      x # 2 cycles
c   	 x      x      x      x      x 
c   0x0021 0x0008 0x001f 0xffff 0x0007
c   	 x      x      x      x      x # 3 cycles
c   	 x      x      x      x      x 
c   	 x      x      x      x      x 
c   0x0021 0x0008 0x001f 0xffff 0x0008
c   	 x      x      x      x      x # 3 cycles
c   	 x      x      x      x      x 
c   	 x      x      x      x      x 
c   0x0021 0x0008 0x001f 0xffff 0x0009
c   	 x      x      x      x      x # 3 cycles
c   	 x      x      x      x      x 
c   	 x      x      x      x      x 
c   0x0021 0x0008 0x001f 0xffff 0x000a
c   	 x      x      x      x      x # 2 cycles
c   	 x      x      x      x      x 
c   0x0021 0x0008 0x0001 0xffff 0x000b
c   	 x      x      x      x      x # 3 cycles
c   	 x      x      x      x      x 
c   	 x      x      x      x      x 
c   0x0021 0x0008 0x0001 0xfffe 0x000c
c   	 x      x      x      x      x # 3 cycles
c   	 x      x      x      x      x 
c   	 x      x      x      x      x 
c   0x0021 0x0008 0x0001 0xfffe 0x000d
c   	 x      x      x      x      x # 3 cycles
c   	 x      x      x      x      x 
c   	 x      x      x      x      x 
c   0x000f 0x0008 0x0001 0xfffe 0x000e
c   	 x      x      x      x      x # 3 cycles
c   	 x      x      x      x      x 
c   	 x      x      x      x      x 
c   0x000f 0x0008 0x0001 0xfffd 0x000f
c   	 x      x      x      x      x # 3 cycles
c   	 x      x      x      x      x 
c   	 x      x      x      x      x 
c   0x000f 0x0008 0x0001 0xfffd 0x0010
c   	 x      x      x      x      x # 3 cycles
c   	 x      x      x      x      x 
c   	 x      x      x      x      x 
c   0x000f 0x0007 0x0001 0xfffd 0x0011
c   	 x      x      x      x      x # 3 cycles
c   	 x      x      x      x      x 
c   	 x      x      x      x      x 
c   0xfffe 0x0007 0x0001 0xfffd 0x0012
c   	 x      x      x      x      x # 3 cycles
c   	 x      x      x      x      x 
c   	 x      x      x      x      x 
c   0x0021 0x0007 0x0001 0xfffd 0x0013
c   	 x      x      x      x      x # 3 cycles
c   	 x      x      x      x      x 
c   	 x      x      x      x      x 
c   0x0022 0x0007 0x0001 0xfffd 0x0014
c   	 x      x      x      x      x # 3 cycles
c   	 x      x      x      x      x 
c   	 x      x      x      x      x 
c   0x0022 0x0007 0x0001 0xfffc 0x0015
c   	 x      x      x      x      x # 2 cycles
c   	 x      x      x      x      x 
c   0x0022 0x0007 0x0018 0xfffc 0x0016
c   	 x      x      x      x      x # 3 cycles
c   	 x      x      x      x      x 
c   	 x      x      x      x      x 
c   0x0022 0x0007 0x0018 0xfffc 0x0017
c   	 x      x      x      x      x # 2 cycles
c   	 x      x      x      x      x 
c 0x0022 0x0007 0x0018 0xfffc 0x0008
c x x x x x
c x x x x x
c x x x x x
c   0x0022 0x0007 0x0018 0xfffc 0x0009
c x x x x x
c x x x x x
c x x x x x
c   0x0022 0x0007 0x0018 0xfffc 0x000a
c x x x x x
c x x x x x
c   0x0022 0x0007 0x0001 0xfffc 0x000b
c x x x x x
c x x x x x
c x x x x x
c   0x0022 0x0007 0x0001 0xfffb 0x000c
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*/

/* Test case SUB:
CLK     R1     R2     R3     R4     PC

init R4=0x27;
init R2=0x93;
c        x      x      x      x 0x0000 # overhead
c        x      x      x      x      x # 3 Cycles each
c   	 x      x      x      x      x
c   	 x      x      x      x      x
c   0xff94 0x0093      x 0x0027 0x0001
c        x      x      x      x      x # 3 Cycles each
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*/

/* Test case MEM:
CLK     R1     R2     R3     R4     PC

c        x      x      x      x 0x0000 # overhead
c        x      x      x      x      x # 2 Cycles I-Mem
c   	 x      x      x      x      x
c   0x000a      x      x      x 0x0001
c        x      x      x      x      x # 3 Cycles ALU
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*/

/* Test case AND:
CLK     R1     R2     R3     R4     PC

init R1=0xF0AE;
init R3=0x0FCF;
c        x      x      x      x 0x0000 # overhead
c        x      x      x      x      x # 3 Cycles each
c   	 x      x      x      x      x
c   	 x      x      x      x      x
c   0xf0ae      x 0x0fcf 0x008e 0x0001
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*/

/* Test case FIB:
CLK     R1     R2     R3     R4   FLAG     PC

declare FLAG = FL & 0xF;

c        x      x      x      x      x 0x0000 # overhead
c        x      x      x      x      x      x # 2 Cycles I-Mem
c   	 x      x      x      x      x      x
c   0x0001      x      x      x      x 0x0001
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*/

/* Test case XOR:
CLK     R1     R2     R3     R4     PC

init R4=0xF0AE;
init R3=0x0FC8;
c        x      x      x      x 0x0000 # overhead
c        x      x      x      x      x # 3 Cycles each
c   	 x      x      x      x      x
c   	 x      x      x      x      x
c   0xff66      x 0x0fc8 0xf0ae 0x0001
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*/

/* Test case COND:
CLK     R1     R2     R3     R4     PC

c        x      x      x      x 0x0000 # overhead 0x0100
c        x      x      x      x      x # 2 Cycles I-Mem
c   	 x      x      x      x      x
c   0x0000      x      x      x 0x0001 # 0x0200
c        x      x      x      x      x # 2 Cycles I-Mem
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*/
