// Digital circuit extended-reg_file.dig as structural Verilog
module extended_reg_file (
  input  [2:0] WS,
  input  WE,
  input  [2:0] RS1,
  input  [2:0] RS2,
  input  [15:0] IN,
  input  clk,
  input  [3:0] Flags,
  output [15:0] OUT1,
  output [15:0] PC,
  output [15:0] OUT2
);

  wire demultiplexer_2_out_1, demultiplexer_2_out_2, demultiplexer_2_out_3, demultiplexer_2_out_4,
       demultiplexer_2_out_6;
  wire [15:0] demultiplexer_1_out_0, demultiplexer_1_out_1, demultiplexer_1_out_2, demultiplexer_1_out_3,
       demultiplexer_1_out_4, demultiplexer_1_out_6, FL_q, NUNYA_s, R1_q, R2_q, R3_q, R4_q, register_1_q;

  Demultiplexer #(.Selector_Bits(3), .Bits(16)) demultiplexer_1 (
    .sel(WS), .in(IN), .out_0(demultiplexer_1_out_0), .out_1(demultiplexer_1_out_1),
    .out_2(demultiplexer_1_out_2), .out_3(demultiplexer_1_out_3), .out_4(demultiplexer_1_out_4),
    .out_6(demultiplexer_1_out_6));  // open: out_5, out_7
  Demultiplexer #(.Selector_Bits(3)) demultiplexer_2 (
    .sel(WS), .in(WE), .out_1(demultiplexer_2_out_1), .out_2(demultiplexer_2_out_2),
    .out_3(demultiplexer_2_out_3), .out_4(demultiplexer_2_out_4), .out_6(demultiplexer_2_out_6));  // open: out_0, out_5, out_7
  Register #(.Bits(16)) register_1 (.D({16{1'b0}}), .C(clk), .en(1'b0), .Q(register_1_q));
  Register #(.Bits(16)) R1 (.D(demultiplexer_1_out_1), .C(clk), .en(demultiplexer_2_out_1), .Q(R1_q));
  Register #(.Bits(16)) R2 (.D(demultiplexer_1_out_2), .C(clk), .en(demultiplexer_2_out_2), .Q(R2_q));
  Register #(.Bits(16)) R3 (.D(demultiplexer_1_out_3), .C(clk), .en(demultiplexer_2_out_3), .Q(R3_q));
  Register #(.Bits(16)) R4 (.D(demultiplexer_1_out_4), .C(clk), .en(demultiplexer_2_out_4), .Q(R4_q));
  Register #(.Bits(16)) FL (.D({{12{1'b0}}, Flags}), .C(clk), .en(1'b1), .Q(FL_q));
  Register #(.Bits(16), .isProgramCounter("true")) u_PC (
    .D(demultiplexer_1_out_6), .C(clk), .en(demultiplexer_2_out_6), .Q(PC));
  Sub #(.Bits(16)) NUNYA (.a(PC), .b({16{1'b0}}), .c_i(1'b1), .s(NUNYA_s));  // open: c_o
  Multiplexer #(.Selector_Bits(3), .Bits(16)) multiplexer_1 (
    .sel(RS2), .in_0(register_1_q), .in_1(R1_q), .in_2(R2_q), .in_3(R3_q), .in_4(R4_q), .in_5(FL_q),
    .in_6(NUNYA_s), .in_7({16{1'b0}}), .out(OUT2));
  Multiplexer #(.Selector_Bits(3), .Bits(16)) multiplexer_2 (
    .sel(RS1), .in_0(register_1_q), .in_1(R1_q), .in_2(R2_q), .in_3(R3_q), .in_4(R4_q), .in_5(FL_q),
    .in_6(NUNYA_s), .in_7({16{1'b0}}), .out(OUT1));

  // Notes on the sheet:
  //   WS: The index of the register which should save the value on IN on the next clock cycle (if WE is high).
  //   WE: Whether the register selected by WS should save the value from IN on the next cycle.
  //   RS1: The index of the register which should output its value to OUT1.
  //   RS2: The index of the register which should output its value to OUT2.
  //   OUT1: The value in the register specified by RS1.
  //   IN: The value to be saved into the register specified by WS if WE is high,
  //   OUT2: The value in the register specified by RS2.
  //   For backwards Comp
  //   FL in control unit used for conditions
  //   this only exists for reading as per 
  //   QUAC
  //   PC should be on datapath not here
  //   It also shouldn't need a subtracter
  //   but incrementing once in fetch is
  //   better than at the end of mult. instr.
  //   "What's Nunya?"
  //   Nunya Business mate
endmodule

/* Test case:
clk RS1 RS2 WS WE IN OUT1 OUT2
c 0 0 0 1 0x1234 0x0000 0x0000
c 1 0 1 1 0xBEEF 0xBEEF 0x0000
c 2 1 2 1 0xDEAD 0xDEAD 0xBEEF
c 3 2 3 1 0xFFFF 0xFFFF 0xDEAD
c 3 2 3 0 0xABCD 0xFFFF 0xDEAD
c 3 2 2 0 0xABCD 0xFFFF 0xDEAD
c 1 0 1 0 0xABCD 0xBEEF 0x0000
c 1 0 0 0 0xABCD 0xBEEF 0x0000
c 1 0 2 1 0xBADE 0xBEEF 0x0000
c 0 2 2 1 0xBADE 0x0000 0xBADE
c 0 0 2 0 0x1234 0x0000 0x0000
c 2 3 0 1 0x0000 0xBADE 0xFFFF
c 0 0 2 0 0x1234 0x0000 0x0000
c 4 4 4 1 0x1234 0x1234 0x1234
*/
