// Digital circuit reg_file.dig as structural Verilog
module reg_file (
  input  [15:0] FLAGS,
  input  [15:0] IN,
  input  [2:0] RS1,
  input  [2:0] RS2,
  input  [2:0] WS,
  input  WE,
  input  FLEN,
  input  SETH,
  input  clk,
  output [15:0] OUT1,
  output [15:0] OUT2,
  output [15:0] FLGS,
  output [15:0] PC
);

  wire demultiplexer_2_out_1, demultiplexer_2_out_2, demultiplexer_2_out_3, demultiplexer_2_out_4,
       demultiplexer_2_out_6;
  wire [15:0] add_1_s, demultiplexer_1_out_1, demultiplexer_1_out_2, demultiplexer_1_out_3,
       demultiplexer_1_out_4, demultiplexer_1_out_6, multiplexer_1_out, multiplexer_2_out, multiplexer_3_out,
       R1_q, R2_q, R3_q, R4_q, register_1_q;

  Multiplexer #(.Bits(16)) multiplexer_1 (
    .sel(SETH), .in_0(IN), .in_1({IN[7:0], multiplexer_3_out[7:0]}), .out(multiplexer_1_out));
  Demultiplexer #(.Selector_Bits(3), .Bits(16)) demultiplexer_1 (
    .sel(WS), .in(multiplexer_1_out), .out_1(demultiplexer_1_out_1), .out_2(demultiplexer_1_out_2),
    .out_3(demultiplexer_1_out_3), .out_4(demultiplexer_1_out_4), .out_6(demultiplexer_1_out_6));  // open: out_0, out_5, out_7
  Multiplexer #(.Bits(16)) multiplexer_2 (
    .sel(demultiplexer_2_out_6), .in_0(add_1_s), .in_1(demultiplexer_1_out_6), .out(multiplexer_2_out));
  Demultiplexer #(.Selector_Bits(3)) demultiplexer_2 (
    .sel(WS), .in(WE), .out_1(demultiplexer_2_out_1), .out_2(demultiplexer_2_out_2),
    .out_3(demultiplexer_2_out_3), .out_4(demultiplexer_2_out_4), .out_6(demultiplexer_2_out_6));  // open: out_0, out_5, out_7
  Add #(.Bits(16)) add_1 (.a({16{1'b0}}), .b(PC), .c_i(1'b1), .s(add_1_s));  // open: c_o
  Register #(.Bits(16)) register_1 (.D({16{1'b0}}), .C(clk), .en(1'b0), .Q(register_1_q));
  Register #(.Bits(16)) R1 (.D(demultiplexer_1_out_1), .C(clk), .en(demultiplexer_2_out_1), .Q(R1_q));
  Register #(.Bits(16)) R2 (.D(demultiplexer_1_out_2), .C(clk), .en(demultiplexer_2_out_2), .Q(R2_q));
  Register #(.Bits(16)) R3 (.D(demultiplexer_1_out_3), .C(clk), .en(demultiplexer_2_out_3), .Q(R3_q));
  Register #(.Bits(16)) R4 (.D(demultiplexer_1_out_4), .C(clk), .en(demultiplexer_2_out_4), .Q(R4_q));
  Register #(.Bits(16)) FL (.D(FLAGS), .C(clk), .en(FLEN), .Q(FLGS));
  Register #(.Bits(16), .isProgramCounter("true")) u_PC (.D(multiplexer_2_out), .C(clk), .en(1'b1), .Q(PC));
  Multiplexer #(.Selector_Bits(3), .Bits(16)) multiplexer_3 (
    .sel(WS), .in_0(register_1_q), .in_1(R1_q), .in_2(R2_q), .in_3(R3_q), .in_4(R4_q), .in_5(FLGS),
    .in_6(PC), .in_7({16{1'b0}}), .out(multiplexer_3_out));
  Multiplexer #(.Selector_Bits(3), .Bits(16)) multiplexer_4 (
    .sel(RS2), .in_0(register_1_q), .in_1(R1_q), .in_2(R2_q), .in_3(R3_q), .in_4(R4_q), .in_5(FLGS),
    .in_6(PC), .in_7({16{1'b0}}), .out(OUT2));
  Multiplexer #(.Selector_Bits(3), .Bits(16)) multiplexer_5 (
    .sel(RS1), .in_0(register_1_q), .in_1(R1_q), .in_2(R2_q), .in_3(R3_q), .in_4(R4_q), .in_5(FLGS),
    .in_6(PC), .in_7({16{1'b0}}), .out(OUT1));

  // Notes on the sheet:
  //   IN: The value to be saved into the register specified by WS if WE is high,
  //   RS1: The index of the register which should output its value to OUT1.
  //   RS2: The index of the register which should output its value to OUT2.
  //   WS: The index of the register which should save the value on IN on the next clock cycle (if WE is high).
  //   OUT1: The value in the register specified by RS1.
  //   OUT2: The value in the register specified by RS2.
  //   WE: Whether the register selected by WS should save the value from IN on the next cycle.
  //   If WE, str data, else, inc
endmodule

/* Test case:
clk RS1 RS2 WS WE IN OUT1 OUT2
c 0 0 0 1 0x1234 0x0000 0x0000
c 1 0 1 1 0xBEEF 0xBEEF 0x0000
c 2 1 2 1 0xDEAD 0xDEAD 0xBEEF
c 3 2 3 1 0xFFFF 0xFFFF 0xDEAD
c 3 2 3 0 0xABCD 0xFFFF 0xDEAD
c 3 2 2 0 0xABCD 0xFFFF 0xDEAD
c 1 0 1 0 0xABCD 0xBEEF 0x0000
c 1 0 0 0 0xABCD 0xBEEF 0x0000
c 1 0 2 1 0xBADE 0xBEEF 0x0000
c 0 2 2 1 0xBADE 0x0000 0xBADE
c 0 0 2 0 0x1234 0x0000 0x0000
c 2 3 0 1 0x0000 0xBADE 0xFFFF
c 0 0 2 0 0x1234 0x0000 0x0000
c 4 4 4 1 0x1234 0x1234 0x1234
*/
